# Fritzing sketch Parkhaussteuerung_Schaltskizze (saved by Fritzing 0.9.10b)
breadboards: 1

parts:
  Bauteil1 = Arduino Uno (Rev3)
  Ultraschallsensor_(Einfahrt) = HC-SR04 Ultrasonic Distance Sensor
  Ultraschallsensor_(Ausfahrt) = HC-SR04 Ultrasonic Distance Sensor
  Servomotor_Schranke = Basic Servo
  OLED_(SSD1306) = Grove OLED 128x96

nets:
  N1: Bauteil1.D8, Ultraschallsensor_(Ausfahrt).ECHO
  N2: Bauteil1.D9_PWM, Servomotor_Schranke.gnd
  N3: Bauteil1.D12/MISO, Ultraschallsensor_(Einfahrt).TRIG
  N4: Bauteil1.D13/SCK, Ultraschallsensor_(Einfahrt).ECHO
  N5: Bauteil1.A4/SDA, OLED_(SSD1306).SDA
  N6: Bauteil1.A5/SCL, OLED_(SSD1306).SCL
  N7: Bauteil1.D7, Ultraschallsensor_(Ausfahrt).TRIG
  VCC: Bauteil1.5V, Ultraschallsensor_(Einfahrt).VCC, Ultraschallsensor_(Ausfahrt).VCC, Servomotor_Schranke.vcc, OLED_(SSD1306).VCC
  GND: Bauteil1.GND, Ultraschallsensor_(Einfahrt).GND, Ultraschallsensor_(Ausfahrt).GND, Servomotor_Schranke.pulse, OLED_(SSD1306).GND
